# Fritzing sketch diagram (saved by Fritzing 0.9.2b)
breadboards: 1

parts:
  Raspberry_Pi1 = Raspberry Pi B rev2
  DI1 = 7-Segment LED Display [package=THT]
  R1 = Resistor [tolerance=±5% resistance=220 package=THT]
  R2 = Resistor [tolerance=±5% resistance=220 package=THT]  # not connected

nets:
  N1: Raspberry_Pi1.3V3, DI1.cathodeE
  N2: Raspberry_Pi1.GPIO_24, DI1.cathodeG
  N3: Raspberry_Pi1.GPIO_10, DI1.cathodeD
  N4: Raspberry_Pi1.GPIO_9, DI1.cathodeC
  N5: Raspberry_Pi1.GPIO_25, DI1.cathodeF
  N6: Raspberry_Pi1.GPIO_11, DI1.cathodeDP
  N7: Raspberry_Pi1.GPIO_8, DI1.cathodeA
  N8: Raspberry_Pi1.GPIO_7, DI1.cathodeB
  N9: DI1.commAnode#7, R1.Pin_1
