# Fritzing sketch diagram (saved by Fritzing 0.9.2b)
breadboards: 1

parts:
  Raspberry_Pi1 = Raspberry Pi B rev2
  DI1 = 7-Segment LED Display [package=THT]
  S1 = Pushbutton [package="[THT]"]
  S2 = Pushbutton [package="[THT]"]
  R1 = Resistor [tolerance=±5% resistance=220 package=THT]
  R2 = Resistor [tolerance=±5% resistance=220 package=THT]  # not connected
  R3 = Resistor [tolerance=±5% resistance=220 package=THT]
  R4 = Resistor [tolerance=±5% resistance=220 package=THT]

nets:
  N1: Raspberry_Pi1.3V3, DI1.cathodeE
  N2: Raspberry_Pi1.GND, R3.Pin_0, R4.Pin_0
  N3: Raspberry_Pi1.GPIO_17, S1.Pin_3, S1.Pin_4
  N4: Raspberry_Pi1.GPIO_27, S2.Pin_3, S2.Pin_4
  N5: Raspberry_Pi1.GPIO_24, DI1.cathodeG
  N6: Raspberry_Pi1.GPIO_10, DI1.cathodeD
  N7: Raspberry_Pi1.GPIO_9, DI1.cathodeC
  N8: Raspberry_Pi1.GPIO_25, DI1.cathodeF
  N9: Raspberry_Pi1.GPIO_11, DI1.cathodeDP
  N10: Raspberry_Pi1.GPIO_8, DI1.cathodeA
  N11: Raspberry_Pi1.GPIO_7, DI1.cathodeB
  N12: DI1.commAnode#7, R1.Pin_1
  N13: S1.Pin_1, S1.Pin_2, R4.Pin_1
  N14: S2.Pin_1, S2.Pin_2, R3.Pin_1
