# Fritzing sketch diagram (saved by Fritzing 0.9.2b)
breadboards: 1

parts:
  U1 = 74HC595 SMD [package="SO16 [SMD]"]
  LED1 = LED - 5mm [color="Red (633nm)" package="5 mm [THT]"]
  R1 = Resistor [tolerance=±5% resistance=220 package=THT]
  LED2 = LED - 5mm [color="Red (633nm)" package="5 mm [THT]"]
  R2 = Resistor [tolerance=±5% resistance=220 package=THT]
  R3 = Resistor [tolerance=±5% resistance=220 package=THT]
  LED3 = LED - 5mm [color="Red (633nm)" package="5 mm [THT]"]
  R4 = Resistor [tolerance=±5% resistance=220 package=THT]
  LED4 = LED - 5mm [color="Red (633nm)" package="5 mm [THT]"]
  R5 = Resistor [tolerance=±5% resistance=220 package=THT]
  LED5 = LED - 5mm [color="Red (633nm)" package="5 mm [THT]"]
  R6 = Resistor [tolerance=±5% resistance=220 package=THT]
  LED6 = LED - 5mm [color="Red (633nm)" package="5 mm [THT]"]
  R7 = Resistor [tolerance=±5% resistance=220 package=THT]
  LED7 = LED - 5mm [color="Red (633nm)" package="5 mm [THT]"]
  R8 = Resistor [tolerance=±5% resistance=220 package=THT]
  LED8 = LED - 5mm [color="Red (633nm)" package="5 mm [THT]"]
  Raspberry_Pi1 = Raspberry Pi B rev2

nets:
  N1: U1.Q1, LED7.anode
  N2: U1.Q2, LED6.anode
  N3: U1.Q3, LED5.anode
  N4: U1.Q4, LED4.anode
  N5: U1.Q5, LED3.anode
  N6: U1.Q6, LED2.anode
  N7: U1.Q7, LED1.anode
  GND: U1.GND, U1.OE, R1.Pin_0, R2.Pin_0, R3.Pin_0, R4.Pin_0, R5.Pin_0, R6.Pin_0, R7.Pin_0, R8.Pin_0, Raspberry_Pi1.GND
  VCC: U1.MR, U1.VCC, Raspberry_Pi1.3V3
  N8: U1.SH_CP, Raspberry_Pi1.GPIO_7
  N9: U1.ST_CP, Raspberry_Pi1.GPIO_25
  N10: U1.DS, Raspberry_Pi1.GPIO_8
  N11: U1.Q0, LED8.anode
  N12: LED1.cathode, R1.Pin_1
  N13: LED2.cathode, R2.Pin_1
  N14: R3.Pin_1, LED3.cathode
  N15: R4.Pin_1, LED4.cathode
  N16: R5.Pin_1, LED5.cathode
  N17: R6.Pin_1, LED6.cathode
  N18: R7.Pin_1, LED7.cathode
  N19: R8.Pin_1, LED8.cathode
