# Fritzing sketch diagram (saved by Fritzing 0.9.2b)
breadboards: 1

parts:
  R1 = Resistor [tolerance=±5% resistance=270 package=THT]
  Raspberry_Pi_B_rev1 = Raspberry Pi B rev1
  R2 = Resistor [tolerance=±5% resistance=270 package=THT]
  R3 = Resistor [tolerance=±5% resistance=270 package=THT]
  LED1 = LED - 5mm [color="Green (555nm)" package="5 mm [THT]"]
  LED2 = LED - 5mm [color="Yellow (592nm)" package="5 mm [THT]"]
  LED3 = LED - 5mm [color="Red (633nm)" package="5 mm [THT]"]

nets:
  N1: R1.Pin_0, LED1.cathode
  N2: R1.Pin_1, Raspberry_Pi_B_rev1.GND, R2.Pin_1, R3.Pin_1
  N3: Raspberry_Pi_B_rev1.GPIO_23, LED3.anode
  N4: Raspberry_Pi_B_rev1.GPIO_21, LED1.anode
  N5: Raspberry_Pi_B_rev1.GPIO_22, LED2.anode
  N6: R2.Pin_0, LED2.cathode
  N7: R3.Pin_0, LED3.cathode
