# Fritzing sketch diagram (saved by Fritzing 0.9.2b)
breadboards: 1

parts:
  LED1 = LED - 5mm [color="Green (555nm)" package="5 mm [THT]"]
  S1 = Pushbutton [package="[THT]"]
  R1 = Resistor [tolerance=±5% resistance=220 package=THT]
  Raspberry_Pi1 = Raspberry Pi B rev2

nets:
  N1: LED1.cathode, R1.Pin_1
  N2: LED1.anode, Raspberry_Pi1.GPIO_17
  N3: S1.Pin_1, S1.Pin_2, Raspberry_Pi1.GPIO_4
  N4: S1.Pin_3, S1.Pin_4, R1.Pin_0, Raspberry_Pi1.GND
