# Fritzing sketch diagram (saved by Fritzing 0.9.2b)
breadboards: 1

parts:
  LED1 = LED - 5mm [color="Blue (470nm)" package="5 mm [THT]"]
  R1 = Resistor [tolerance=±5% resistance=220 package=THT]
  Raspberry_Pi1 = Raspberry Pi B rev2

nets:
  N1: LED1.cathode, R1.Pin_1
  N2: LED1.anode, Raspberry_Pi1.GPIO_14
  N3: R1.Pin_0, Raspberry_Pi1.GND
