# Fritzing sketch diagram (saved by Fritzing 0.9.2b)
breadboards: 1

parts:
  LED1 = RGB LED (com. cathode, rbg) [package="5 mm [THT]"]  # not connected
  S1 = Pushbutton [package="[THT]"]
  R1 = Resistor [tolerance=±5% resistance=220 package=THT]
  R2 = Resistor [tolerance=±5% resistance=220 package=THT]
  R3 = Resistor [tolerance=±5% resistance=220 package=THT]
  R4 = Resistor [tolerance=±5% resistance=220 package=THT]
  R5 = Resistor [tolerance=±5% resistance=220 package=THT]
  R6 = Resistor [tolerance=±5% resistance=220 package=THT]
  S2 = Pushbutton [package="[THT]"]
  S3 = Pushbutton [package="[THT]"]

nets:
  N1: S1.Pin_1, S1.Pin_2, R1.Pin_0, R2.Pin_0, R3.Pin_0
  N2: S1.Pin_3, S1.Pin_4
  N3: R1.Pin_1, R2.Pin_1, R3.Pin_1, R4.Pin_1, R5.Pin_1, R6.Pin_1
  N4: R4.Pin_0, R5.Pin_0, S3.Pin_1, S3.Pin_2
  N5: R6.Pin_0, S2.Pin_1, S2.Pin_2
  N6: S2.Pin_3, S2.Pin_4
  N7: S3.Pin_3, S3.Pin_4

notes:
  GND
  3v3
