# Fritzing sketch diagram (saved by Fritzing 0.9.2b)
breadboards: 1

parts:
  LED1 = LED - 5mm [color="White (6500K)" package="5 mm [THT]"]
  S1 = Pushbutton [package="[THT]"]
  R1 = Resistor [tolerance=±5% resistance=220 package=THT]
  Raspberry_Pi1 = Raspberry Pi B rev2
  LED2 = LED - 5mm [color="Green (555nm)" package="5 mm [THT]"]
  LED3 = LED - 5mm [color="Yellow (585nm)" package="5 mm [THT]"]
  LED4 = LED - 5mm [color="Red (633nm)" package="5 mm [THT]"]
  R2 = Resistor [tolerance=±5% resistance=220 package=THT]
  R3 = Resistor [tolerance=±5% resistance=220 package=THT]
  R4 = Resistor [tolerance=±5% resistance=220 package=THT]

nets:
  N1: LED1.cathode, R1.Pin_1
  N2: LED1.anode, Raspberry_Pi1.GPIO_14
  N3: S1.Pin_1, S1.Pin_2, Raspberry_Pi1.GPIO_4
  N4: S1.Pin_3, S1.Pin_4, R1.Pin_0, Raspberry_Pi1.GND, R2.Pin_0, R3.Pin_0, R4.Pin_0
  N5: Raspberry_Pi1.GPIO_23, LED2.cathode
  N6: Raspberry_Pi1.GPIO_24, LED3.cathode
  N7: Raspberry_Pi1.GPIO_25, LED4.cathode
  N8: LED2.anode, R2.Pin_1
  N9: LED3.anode, R3.Pin_1
  N10: LED4.anode, R4.Pin_1
